// Logisim project Proj_1_HF26.circ as structural Verilog
module main (
);

  wire clock_1_out, dec_counter_1__0, dec_counter_1__1, dec_counter_1__2, dec_counter_1__3;

  Clock clock_1 (.out(clock_1_out));
  dec_counter dec_counter_1 (
    .Clock(clock_1_out), ._0(dec_counter_1__0), ._1(dec_counter_1__1), ._2(dec_counter_1__2),
    ._3(dec_counter_1__3));  // open: IS_NINE
  // NOT_Gate not_1 has open pins: in=dec_counter_1__0, out=open
  // NOT_Gate not_2 has open pins: in=dec_counter_1__1, out=open
  // NOT_Gate not_3 has open pins: in=dec_counter_1__2, out=open
  // NOT_Gate not_4 has open pins: in=dec_counter_1__3, out=open
  _7_Segment_Display u_7_segment_display_1 ();  // open: g, f, a, b, e, d, c, dp
endmodule

module bonus (
);

  wire clock_1_out;

  Clock clock_1 (.out(clock_1_out));
  hex_counter hex_counter_1 (.Clock(clock_1_out));  // open: IS_FIFTEEN, _0, _1, _2, _3
  _7_Segment_Display u_7_segment_display_1 ();  // open: g, f, a, b, e, d, c, dp
endmodule

module dec_counter (
  input  Clock,
  output _0,
  output _1,
  output _2,
  output _3,
  output IS_NINE
);

  wire and_2_out, and_3_out, and_4_out, and_5_out, and_6_out, and_7_out, and_8_out, D1_qn, D2_qn, D3_qn,
       D4_qn, or_1_out, or_2_out, or_3_out;

  and and_1 (IS_NINE, _3, D2_qn, D3_qn, _0);
  and and_2 (and_2_out, _3, D4_qn);
  and and_3 (and_3_out, _2, _1, _0);
  and and_4 (and_4_out, _2, D3_qn);
  and and_5 (and_5_out, _2, D4_qn);
  and and_6 (and_6_out, D2_qn, _1, _0);
  and and_7 (and_7_out, _1, D4_qn);
  and and_8 (and_8_out, D1_qn, D3_qn, _0);
  or or_1 (or_1_out, and_2_out, and_3_out);
  or or_2 (or_2_out, and_4_out, and_5_out, and_6_out);
  or or_3 (or_3_out, and_7_out, and_8_out);
  D_Flip_Flop #(.trigger("falling")) D1 (.clk(Clock), .D(or_1_out), .Q(_3), .Qn(D1_qn));  // open: preset, en, reset
  D_Flip_Flop #(.trigger("falling")) D2 (.clk(Clock), .D(or_2_out), .Q(_2), .Qn(D2_qn));  // open: preset, en, reset
  D_Flip_Flop #(.trigger("falling")) D3 (.clk(Clock), .D(or_3_out), .Q(_1), .Qn(D3_qn));  // open: preset, en, reset
  D_Flip_Flop #(.trigger("falling")) D4 (.clk(Clock), .D(D4_qn), .Q(_0), .Qn(D4_qn));  // open: preset, en, reset
endmodule

module hex_counter (
  input  Clock,
  output _0,
  output _1,
  output _2,
  output _3,
  output IS_FIFTEEN
);

  wire and_2_out, and_3_out, and_4_out, and_5_out, and_6_out, and_7_out, and_8_out, and_9_out, and_10_out,
       D1_qn, D2_qn, D3_qn, D4_qn, or_1_out, or_2_out, or_3_out;

  and and_1 (IS_FIFTEEN, _3, _2, _1, _0);
  and and_2 (and_2_out, _3, D2_qn);
  and and_3 (and_3_out, _3, D3_qn);
  and and_4 (and_4_out, _3, D4_qn);
  and and_5 (and_5_out, D1_qn, _2, _1, _0);
  and and_6 (and_6_out, _2, D3_qn);
  and and_7 (and_7_out, _2, D4_qn);
  and and_8 (and_8_out, D2_qn, _1, _0);
  and and_9 (and_9_out, _1, D4_qn);
  and and_10 (and_10_out, D3_qn, _0);
  or or_1 (or_1_out, and_2_out, and_3_out, and_4_out, and_5_out);
  or or_2 (or_2_out, and_6_out, and_7_out, and_8_out);
  or or_3 (or_3_out, and_9_out, and_10_out);
  D_Flip_Flop #(.trigger("falling")) D1 (.clk(Clock), .D(or_1_out), .Q(_3), .Qn(D1_qn));  // open: preset, en, reset
  D_Flip_Flop #(.trigger("falling")) D2 (.clk(Clock), .D(or_2_out), .Q(_2), .Qn(D2_qn));  // open: preset, en, reset
  D_Flip_Flop #(.trigger("falling")) D3 (.clk(Clock), .D(or_3_out), .Q(_1), .Qn(D3_qn));  // open: preset, en, reset
  D_Flip_Flop #(.trigger("falling")) D4 (.clk(Clock), .D(D4_qn), .Q(_0), .Qn(D4_qn));  // open: preset, en, reset
endmodule
